// Logisim project s-mips.circ as structural Verilog: 31 circuits, main circuit S-MIPS Board
module RAM (
  input  [15:0] Address,
  input  [31:0] Data_In_0,
  input  [31:0] Data_In_1,
  input  [31:0] Data_In_2,
  input  [31:0] Data_In_3,
  input  [3:0] Mask,
  input  nRead_Write,
  input  Chip_Select,
  input  Reset,
  output [31:0] Data_Out_0,
  output [31:0] Data_Out_1,
  output [31:0] Data_Out_2,
  output [31:0] Data_Out_3,
  output [3:0] Read_Time,
  output [3:0] Write_Time
);

  wire and_2_out, and_3_out, and_4_out, and_5_out, and_6_out, and_7_out, and_8_out, and_9_out, Changed, CLK,
       comparator_2_eq, comparator_3_eq, comparator_4_eq, comparator_5_eq, comparator_6_eq, Count,
       demultiplexer_3_out0, Idle, Idle_q, Load, Load0, Load1, nand_1_out, or_1_out, or_2_out, or_3_out,
       or_4_out, or_5_out, or_6_out, or_7_out, or_8_out, or_9_out, or_10_out, Proc_q, Update_Mem, Zero_Time;
  wire [3:0] counter_1_q, multiplexer_1_out, subtractor_1_out;
  wire [31:0] register_1_q, register_2_q, register_3_q, register_4_q, register_5_q;

  // Probe on 4'b0011
  // Probe on 4'b0010
  Multiplexer #(.width(4), .enable("false")) multiplexer_1 (
    .in0(4'b0011), .in1(4'b0010), .out(multiplexer_1_out), .sel(nRead_Write));
  or or_1 (or_1_out, Idle, Update_Mem);
  or or_2 (or_2_out, ~Chip_Select, Reset);  // OR_Gate
  Subtractor #(.width(4)) subtractor_1 (.a(multiplexer_1_out), .b(4'b0010), .out(subtractor_1_out));  // open: bin, bout
  D_Flip_Flop u_Idle (.clk(CLK), .D(or_1_out), .Q(Idle_q), .preset(or_2_out));  // open: Qn, en, reset
  Demultiplexer #(.enable("false")) demultiplexer_1 (.out0(Idle), .out1(Load0), .in(Idle_q), .sel(Changed));
  // Probe on counter_1_q
  Counter #(.width(4), .max('hf)) counter_1 (
    .load(Load), .D(subtractor_1_out), .count(Count), .Q(counter_1_q), .clk(CLK), .clr(or_3_out));  // open: carry
  or or_3 (or_3_out, ~Chip_Select, Reset);  // OR_Gate
  Comparator #(.width(4), .mode("unsigned")) comparator_1 (
    .a(4'b0000), .b(counter_1_q), .eq(Zero_Time));  // open: gt, lt
  or or_4 (or_4_out, Count, Load0, Load1);
  Register #(.width(32)) register_1 (.D(Data_In_0), .en(Chip_Select), .Q(register_1_q), .clk(CLK), .clr(or_5_out));
  or or_5 (or_5_out, ~Chip_Select, Reset);  // OR_Gate
  Register #(.width(32)) register_2 (.D(Data_In_1), .en(Chip_Select), .Q(register_2_q), .clk(CLK), .clr(or_6_out));
  or or_6 (or_6_out, ~Chip_Select, Reset);  // OR_Gate
  Register #(.width(32)) register_3 (.D(Data_In_2), .en(Chip_Select), .Q(register_3_q), .clk(CLK), .clr(or_7_out));
  or or_7 (or_7_out, ~Chip_Select, Reset);  // OR_Gate
  Register #(.width(32)) register_4 (.D(Data_In_3), .en(Chip_Select), .Q(register_4_q), .clk(CLK), .clr(or_8_out));
  or or_8 (or_8_out, ~Chip_Select, Reset);  // OR_Gate
  Register #(.width(32)) register_5 (
    .D({{11{1'b1}}, nRead_Write, Mask, Address}), .en(Chip_Select), .Q(register_5_q), .clk(CLK),
    .clr(or_9_out));
  or or_9 (or_9_out, ~Chip_Select, Reset);  // OR_Gate
  D_Flip_Flop Proc (.clk(CLK), .D(or_4_out), .Q(Proc_q), .reset(or_10_out));  // open: Qn, preset, en
  or or_10 (or_10_out, ~Chip_Select, Reset);  // OR_Gate
  Demultiplexer #(.enable("false")) demultiplexer_2 (
    .out0(Count), .out1(Update_Mem), .in(demultiplexer_3_out0), .sel(Zero_Time));
  Demultiplexer #(.enable("false")) demultiplexer_3 (
    .out0(demultiplexer_3_out0), .out1(Load1), .in(Proc_q), .sel(Changed));
  Clock clock_1 (.out(CLK));
  Comparator #(.width(32)) comparator_2 (.a(register_1_q), .b(Data_In_0), .eq(comparator_2_eq));  // open: gt, lt
  Comparator #(.width(32)) comparator_3 (.a(register_2_q), .b(Data_In_1), .eq(comparator_3_eq));  // open: gt, lt
  Comparator #(.width(32)) comparator_4 (.a(register_3_q), .b(Data_In_2), .eq(comparator_4_eq));  // open: gt, lt
  Comparator #(.width(32)) comparator_5 (.a(register_4_q), .b(Data_In_3), .eq(comparator_5_eq));  // open: gt, lt
  Comparator #(.width(32)) comparator_6 (
    .a(register_5_q), .b({{11{1'b1}}, nRead_Write, Mask, Address}), .eq(comparator_6_eq));  // open: gt, lt
  nand nand_1 (nand_1_out, comparator_6_eq, comparator_2_eq, comparator_3_eq, comparator_4_eq, comparator_5_eq);
  and and_1 (Changed, nand_1_out, Chip_Select);
  or or_11 (Load, Count, Load1, Load0);
  and and_2 (and_2_out, Mask[0], Update_Mem, nRead_Write);
  and and_3 (and_3_out, Mask[1], Update_Mem, nRead_Write);
  and and_4 (and_4_out, Mask[2], Update_Mem, nRead_Write);
  and and_5 (and_5_out, Mask[3], Update_Mem, nRead_Write);
  RAM_part #(.addrWidth(16), .dataWidth(32), .bus("separate")) ram_1 (
    .addr(Address), .din(Data_In_0), .data(Data_Out_0), .str(and_2_out), .sel(Chip_Select), .clk(CLK),
    .ld(and_6_out), .clr(Reset));
  and and_6 (and_6_out, ~nRead_Write, Idle);  // AND_Gate
  RAM_part #(.addrWidth(16), .dataWidth(32), .bus("separate")) ram_2 (
    .addr(Address), .din(Data_In_1), .data(Data_Out_1), .str(and_3_out), .sel(Chip_Select), .clk(CLK),
    .ld(and_7_out), .clr(Reset));
  and and_7 (and_7_out, ~nRead_Write, Idle);  // AND_Gate
  RAM_part #(.addrWidth(16), .dataWidth(32), .bus("separate")) ram_3 (
    .addr(Address), .din(Data_In_2), .data(Data_Out_2), .str(and_4_out), .sel(Chip_Select), .clk(CLK),
    .ld(and_8_out), .clr(Reset));
  and and_8 (and_8_out, ~nRead_Write, Idle);  // AND_Gate
  RAM_part #(.addrWidth(16), .dataWidth(32), .bus("separate")) ram_4 (
    .addr(Address), .din(Data_In_3), .data(Data_Out_3), .str(and_5_out), .sel(Chip_Select), .clk(CLK),
    .ld(and_9_out), .clr(Reset));
  and and_9 (and_9_out, ~nRead_Write, Idle);  // AND_Gate

  assign Read_Time = 4'b0011;
  assign Write_Time = 4'b0010;

  // Other names for the same wires on the sheet: M0 = Mask[0]; M1 = Mask[1]; M2 = Mask[2]; M3 = Mask[3];
  //   RW = nRead_Write; CLR = Reset; CS = Chip_Select; Load2 = Count

  // Notes on the sheet:
  //   NO MODIFICAR
  //   excepto quizás los valores RT y WT
  //   BANK0
  //   BANK1
  //   BANK2
  //   BANK3
endmodule

module RAM_Dispatcher (
  input  [3:0] WriteTime,
  input  Clock,
  input  CLR,
  output [31:0] Data,
  output [15:0] Address,
  output [3:0] Mask,
  output Finished,
  output Write
);

  wire demultiplexer_2_out1, demultiplexer_3_out1, End, IDLE_q, IncAddr, Load, or_1_out, or_2_out, While_q,
       WriteEnd;
  wire [3:0] counter_1_q;
  wire [31:0] CurrentAddress_q;

  Counter #(.width(32), .max('hffffffff)) CurrentAddress (
    .count(IncAddr), .Q({CurrentAddress_q[31:18], Address, CurrentAddress_q[1:0]}), .clk(Clock), .clr(CLR));  // open: load, D, carry
  or or_1 (or_1_out, IncAddr, demultiplexer_3_out1, Finished);
  D_Flip_Flop IDLE (.clk(Clock), .D(or_1_out), .Q(IDLE_q), .preset(CLR));  // open: Qn, en, reset
  Demultiplexer #(.enable("false")) demultiplexer_1 (.out0(Load), .out1(Finished), .in(IDLE_q), .sel(End));
  D_Flip_Flop While (.clk(Clock), .D(or_2_out), .Q(While_q), .reset(CLR));  // open: Qn, preset, en
  or or_2 (or_2_out, Write, Load);
  RAM_part #(.addrWidth(18), .dataWidth(32)) ram_1 (
    .addr({Address, CurrentAddress_q[1:0]}), .data(Data), .clk(Clock));  // open: sel, ld, clr
  Demultiplexer #(.enable("false")) demultiplexer_2 (
    .out0(Write), .out1(demultiplexer_2_out1), .in(While_q), .sel(WriteEnd));
  Decoder #(.select(2)) decoder_1 (
    .out0(Mask[0]), .out1(Mask[1]), .out2(Mask[2]), .out3(Mask[3]), .sel(CurrentAddress_q[1:0]));  // open: en
  Demultiplexer #(.enable("false")) demultiplexer_3 (
    .out0(IncAddr), .out1(demultiplexer_3_out1), .in(demultiplexer_2_out1), .sel(End));
  Counter #(.width(4), .max('hf)) counter_1 (
    .load(Load), .D(WriteTime), .count(Write), .Q(counter_1_q), .clk(Clock));  // open: carry, clr
  Comparator #(.width(32)) comparator_1 (.a(Data), .b({32{1'b1}}), .eq(End));  // open: gt, lt
  Comparator #(.width(4)) comparator_2 (.a(4'b0000), .b(counter_1_q), .eq(WriteEnd));  // open: gt, lt

  // Other names for the same wires on the sheet: CLK = Clock; Count = Write; WT[3:0] = WriteTime
endmodule

module S_MIPS_Board (
  input  DESHABILITAR_DISPATCHER,
  output halt
);

  wire button_1_out, CLK, CS, d_ff_1_q, LCLR, LoadRAM, LoadRAMOn, LW, R_R_W, R_W, ram_dispatcher_1_finished,
       RCS, Reset_out, RST, TTY_EN;
  wire [2:0] KDB;
  wire [3:0] LMask, Mask, ram_1_read_time, ram_1_write_time, RMask;
  wire [6:0] KDB_DATA, TTY_DATA;
  wire [15:0] Addr, LAddr, RAddr;
  wire [31:0] I0, I1, I2, I3, LData, ram_1_data_out_0, ram_1_data_out_1, ram_1_data_out_2, ram_1_data_out_3,
       RI0, RI1, RI2, RI3;

  TTY #(.rows(25), .cols(80)) tty_1 (.data(TTY_DATA), .clk(CLK), .we(TTY_EN), .clr(RST));
  not not_1 (LoadRAMOn, ram_dispatcher_1_finished);
  RAM_Dispatcher ram_dispatcher_1 (
    .WriteTime(ram_1_write_time), .Clock(CLK), .Data(LData), .Address(LAddr), .Mask(LMask),
    .Finished(ram_dispatcher_1_finished), .Write(LW), .CLR(LCLR));
  Keyboard #(.buflen(64)) keyboard_1 (.clk(CLK), .re(KDB[0]), .avail(KDB[2]), .data(KDB_DATA));  // open: clr
  RAM ram_1 (
    .Address(RAddr), .Data_Out_0(ram_1_data_out_0), .Data_Out_1(ram_1_data_out_1),
    .Data_Out_2(ram_1_data_out_2), .Data_Out_3(ram_1_data_out_3), .Data_In_0(RI0), .Data_In_1(RI1),
    .Data_In_2(RI2), .Data_In_3(RI3), .Mask(RMask), .nRead_Write(R_R_W), .Chip_Select(RCS),
    .Read_Time(ram_1_read_time), .Reset(button_1_out), .Write_Time(ram_1_write_time));
  Button button_1 (.out(button_1_out));
  D_Flip_Flop d_ff_1 (.clk(CLK), .D(1'b1), .Q(d_ff_1_q), .reset(Reset_out));  // open: Qn, preset, en
  Button Reset (.out(Reset_out));
  S_MIPS s_mips_1 (
    .Kbd_Enable(KDB[0]), .Address(Addr), .Kbd_Clear(KDB[1]), .Kbd_Available(KDB[2]), .RAM_In_0(I0),
    .Kbd_ASCII_Data(KDB_DATA), .RAM_In_1(I1), .TTY_Enable(TTY_EN), .RAM_In_2(I2), .RAM_In_3(I2),
    .TTY_ASCII_Data(TTY_DATA), .Reset(RST), .RAM_Out_0(ram_1_data_out_0), .Clock(CLK),
    .RAM_Out_1(ram_1_data_out_1), .Stop(halt), .RAM_Out_2(ram_1_data_out_2), .RAM_Out_3(ram_1_data_out_3),
    .Mask(Mask), .Read_Time(ram_1_read_time), .Write_Time(ram_1_write_time), .nRead_Write(R_W),
    .Chip_Select(CS));
  D_Flip_Flop d_ff_2 (.clk(CLK), .D(d_ff_1_q), .Qn(LCLR), .reset(Reset_out));  // open: Q, preset, en
  or or_1 (RST, LCLR, LoadRAM);
  Clock clock_1 (.out(CLK));
  Multiplexer #(.width(32), .enable("false")) multiplexer_1 (.in0(I0), .in1(LData), .out(RI0), .sel(LoadRAM));
  Multiplexer #(.width(32), .enable("false")) multiplexer_2 (.in0(I1), .in1(LData), .out(RI1), .sel(LoadRAM));
  Multiplexer #(.width(32), .enable("false")) multiplexer_3 (.in0(I2), .in1(LData), .out(RI2), .sel(LoadRAM));
  Multiplexer #(.width(32), .enable("false")) multiplexer_4 (.in0(I3), .in1(LData), .out(RI3), .sel(LoadRAM));
  and and_1 (LoadRAM, ~DESHABILITAR_DISPATCHER, LoadRAMOn);  // AND_Gate
  Multiplexer #(.width(16), .enable("false")) multiplexer_5 (.in0(Addr), .in1(LAddr), .out(RAddr), .sel(LoadRAM));
  Multiplexer #(.width(4), .enable("false")) multiplexer_6 (.in0(Mask), .in1(LMask), .out(RMask), .sel(LoadRAM));
  Multiplexer #(.enable("false")) multiplexer_7 (.in0(CS), .in1(LW), .out(RCS), .sel(LoadRAM));
  Multiplexer #(.enable("false")) multiplexer_8 (.in0(R_W), .in1(LW), .out(R_R_W), .sel(LoadRAM));

  // Notes on the sheet:
  //   NO MODIFICAR
  //   Keyboard
endmodule

module S_MIPS (
  input  Kbd_Available,
  input  [6:0] Kbd_ASCII_Data,
  input  [31:0] RAM_Out_0,
  input  [31:0] RAM_Out_1,
  input  Reset,
  input  [31:0] RAM_Out_2,
  input  Clock,
  input  [31:0] RAM_Out_3,
  input  [3:0] Read_Time,
  input  [3:0] Write_Time,
  output Kbd_Enable,
  output [15:0] Address,
  output Kbd_Clear,
  output TTY_Enable,
  output [6:0] TTY_ASCII_Data,
  output Stop,
  output [31:0] RAM_In_0,
  output [31:0] RAM_In_1,
  output [31:0] RAM_In_2,
  output [31:0] RAM_In_3,
  output [3:0] Mask,
  output nRead_Write,
  output Chip_Select
);

  InstDec instdec_1 ();  // open: toalu, cte, in_1, Write, push, pop, jr, offset, beq, bne, blez, bgtz, bltz, j, destino
  DataPath datapath_1 ();  // open: Rs, Rt, Rd, clk, cte, alusel, memory, Rs_Rd, ramreg, cte_register, W, R, Output, push, pop
  BranchControl branchcontrol_1 ();  // open: RIN, Sel4_IN, clk, L, R, Output, offIN, destino, beq, bne, blez, bgtz, bltz, j, jr, eq, ne, lez, gtz, ltz

  // Other names for the same wires on the sheet: CLK = Clock; CLR = Reset; CS = Chip_Select;
  //   KBD_AVAIL = Kbd_Available; KBD_CLR = Kbd_Clear; KBD_DATA[6:0] = Kbd_ASCII_Data; RAM_A[15:0] = Address;
  //   RAM_INPUT_0[31:0] = RAM_In_0; RAM_INPUT_1[31:0] = RAM_In_1; RAM_INPUT_2[31:0] = RAM_In_2;
  //   RAM_INPUT_3[31:0] = RAM_In_3; RAM_MASK[3:0] = Mask; RAM_OUTPUT_0[31:0] = RAM_Out_0;
  //   RAM_OUTPUT_1[31:0] = RAM_Out_1; RAM_OUTPUT_2[31:0] = RAM_Out_2; RAM_OUTPUT_3[31:0] = RAM_Out_3;
  //   RW = nRead_Write; TTY_DATA[6:0] = TTY_ASCII_Data

  // Notes on the sheet:
  //   RAM ADDRESS
  //   DATA FROM RAM
  //   DATA TO RAM
  //   DATA WRITE MASK
  //   RAM TIMING
  //   RAM CONTROL
  //   KEYBOARD
  //   TTY
  //   SEQUENCING
endmodule

module DataPath (
  input  ramreg,
  input  push,
  input  pop,
  input  Rs_Rd,
  input  cte_register,
  input  W,
  input  R,
  input  [4:0] Rs,
  input  [4:0] Rt,
  input  [4:0] Rd,
  input  clk,
  input  [31:0] cte,
  input  [3:0] alusel,
  input  [31:0] memory,
  output [31:0] Output
);

  wire [4:0] multiplexer_2_out;
  wire [31:0] alu_1_out_5, multiplexer_1_out, multiplexer_3_out, regfile_1_b;

  Multiplexer #(.width(32), .enable("false")) multiplexer_1 (
    .in0(alu_1_out_5), .in1(memory), .out(multiplexer_1_out), .sel(ramreg));
  Multiplexer #(.width(5), .disabled(0), .enable("false")) multiplexer_2 (
    .in0(Rt), .in1(Rd), .out(multiplexer_2_out), .sel(Rs_Rd));
  RegFile regfile_1 (
    .CLK(clk), .RST(R), .DI(multiplexer_1_out), .RW(W), .LS(multiplexer_2_out), .SA(Rs), .A(Output),
    .B(regfile_1_b), .SB(Rt), .push(push), .pop(pop));
  Multiplexer #(.width(32), .disabled(0), .enable("false")) multiplexer_3 (
    .in0(regfile_1_b), .in1(cte), .out(multiplexer_3_out), .sel(cte_register));
  ALU alu_1 (.A(Output), .B(multiplexer_3_out), .SEL(alusel), .out_5(alu_1_out_5), .clk(clk));

  // Other names for the same wires on the sheet: alus[3:0] = alusel; c = clk; ram[31:0] = memory; RsO[31:0] = Output
endmodule

module InstDec (
  input  [31:0] in_1,
  output jr,
  output [3:0] toalu,
  output push,
  output pop,
  output beq,
  output bne,
  output blez,
  output bgtz,
  output bltz,
  output j,
  output [31:0] cte,
  output [31:0] offset,
  output [25:0] destino,
  output Write
);

  wire \logic , writealu;
  wire [1:0] DECOP;
  wire [3:0] func000000decode_1_output, opdisctinctdecode_1_output;
  wire [4:0] Rd, Rs, Rt, x;
  wire [5:0] FUNC, OP;

  OPDECODE opdecode_1 (.in_1(OP), .Output(DECOP));
  InstSeparator instseparator_1 (.in_1(in_1), .OPcode(OP), .Rs(Rs), .Rt(Rt), .Rd(Rd), .x(x), .FUNCode(FUNC));
  OPDisctinctDECODE opdisctinctdecode_1 (.in_1(OP), .Output(opdisctinctdecode_1_output));
  FUNC000000DECODE func000000decode_1 (.in_1(FUNC), .Output(func000000decode_1_output));
  Multiplexer #(.select(2), .width(4), .enable("false")) multiplexer_1 (
    .in0(func000000decode_1_output), .in1(opdisctinctdecode_1_output), .in2(4'b0000), .in3(4'b0000),
    .out(toalu), .sel(DECOP));
  Writefromalu writefromalu_1 (.in_1(toalu), .write(writealu));
  push_pop push_pop_1 (.OP(DECOP), .FUNC(FUNC), .push(push), .pop(pop));
  branch branch_1 (.in_1(OP), .beq(beq), .bne(bne), .blez(blez), .bgtz(bgtz), .bltz(bltz), .j(j));
  Const const_1 (.in_2(Rd), .in_3(x), .in_4(FUNC), .Output(cte), .\logic (\logic ));
  Offst offst_1 (.in_1(Rd), .in_2(x), .in_3(FUNC), .Output(offset));
  destinosalto destinosalto_1 (.fx(FUNC), .x(x), .Rd(Rd), .Rt(Rt), .Rs(Rs), .Output(destino));
  jr jr_1 (.in_1(toalu), .jr(jr));
  islogic islogic_1 (.in_1(toalu), .islogic(\logic ));
  or or_1 (Write, writealu, pop);
endmodule

module BranchControl (
  input  [31:0] RIN,
  input  Sel4_IN,
  input  clk,
  input  R,
  input  [31:0] offIN,
  input  L,
  input  [25:0] destino,
  input  beq,
  input  eq,
  input  bne,
  input  ne,
  input  blez,
  input  lez,
  input  bgtz,
  input  gtz,
  input  bltz,
  input  ltz,
  input  j,
  input  jr,
  output [31:0] Output
);

  wire b, or_1_out;
  wire [31:0] destinosalto, multiplexer_1_out, multiplexer_2_out;

  Multiplexer #(.width(32), .enable("false")) multiplexer_1 (
    .in0(RIN), .in1(destinosalto), .out(multiplexer_1_out), .sel(j));
  Multiplexer #(.width(32), .enable("false")) multiplexer_2 (
    .in0(multiplexer_1_out), .in1(offIN), .out(multiplexer_2_out), .sel(b));
  destinobuilder destinobuilder_1 (.des(destino), .PC(Output), .Output(destinosalto));
  PC pc_1 (.IN(multiplexer_2_out), .Output(Output), .jr_j(Sel4_IN), .l(L), .clk(clk), .r(R), .cond(b));
  not not_1 (b, or_1_out);
  or or_1 (or_1_out, j, jr);

  // Other names for the same wires on the sheet: PC[31:0] = Output
endmodule

module PC (
  input  [31:0] IN,
  input  l,
  input  clk,
  input  r,
  input  jr_j,
  input  cond,
  output [31:0] Output
);

  wire [31:0] adder_1_out, adder_2_out, multiplexer_1_out, multiplexer_2_out;

  Multiplexer #(.width(32), .enable("false")) multiplexer_1 (
    .in0(adder_2_out), .in1(IN), .out(multiplexer_1_out), .sel(jr_j));
  Register #(.width(32)) register_1 (.D(multiplexer_1_out), .en(l), .Q(Output), .clk(clk), .clr(r));
  Multiplexer #(.width(32), .enable("false")) multiplexer_2 (
    .in0(32'h4), .in1(adder_1_out), .out(multiplexer_2_out), .sel(cond));
  Adder #(.width(32)) adder_1 (.a(IN), .b(32'h4), .out(adder_1_out));  // open: cin, cout
  Adder #(.width(32)) adder_2 (.a(Output), .b(multiplexer_2_out), .out(adder_2_out));  // open: cin, cout

  // Other names for the same wires on the sheet: off[31:0] = IN
endmodule

module RegFile (
  input  CLK,
  input  RST,
  input  [31:0] DI,
  input  push,
  input  pop,
  input  RW,
  input  [4:0] LS,
  input  [4:0] SA,
  input  [4:0] SB,
  output [31:0] A,
  output [31:0] B
);

  wire l0, l1, l2, l3, l4, l5, l6, l7, l8, l9, l10, l11, l12, l13, l14, l15, l16, l17, l18, l19, l20, l21,
       l22, l23, l24, l25, l26, l27, l28, l29, l30, l31;
  wire [31:0] r1, r2, r3, r4, r5, r6, r7, r8, r9, r10, r11, r12, r13, r14, r15, r16, r17, r18, r19, r20, r21,
       r22, r23, r24, r25, r26, r27, r28, r29, r30, r31;

  Demultiplexer #(.select(5), .disabled(0)) demultiplexer_1 (
    .out0(l0), .out1(l1), .out2(l2), .out3(l3), .out4(l4), .out5(l5), .out6(l6), .out7(l7), .out8(l8),
    .out9(l9), .out10(l10), .out11(l11), .out12(l12), .out13(l13), .out14(l14), .out15(l15), .out16(l16),
    .out17(l17), .out18(l18), .out19(l19), .out20(l20), .out21(l21), .out22(l22), .out23(l23), .out24(l24),
    .out25(l25), .out26(l26), .out27(l27), .out28(l28), .out29(l29), .out30(l30), .out31(l31), .in(1'b1),
    .sel(LS), .en(RW));
  Register #(.width(32)) register_1 (.D(DI), .en(l8), .Q(r8), .clk(CLK), .clr(RST));
  Register #(.width(32)) register_2 (.D(DI), .en(l16), .Q(r16), .clk(CLK), .clr(RST));
  Register #(.width(32)) register_3 (.D(DI), .en(l24), .Q(r24), .clk(CLK), .clr(RST));
  Register #(.width(32)) register_4 (.D(DI), .en(l1), .Q(r1), .clk(CLK), .clr(RST));
  Register #(.width(32)) register_5 (.D(DI), .en(l9), .Q(r9), .clk(CLK), .clr(RST));
  Register #(.width(32)) register_6 (.D(DI), .en(l17), .Q(r17), .clk(CLK), .clr(RST));
  Register #(.width(32)) register_7 (.D(DI), .en(l25), .Q(r25), .clk(CLK), .clr(RST));
  Register #(.width(32)) register_8 (.D(DI), .en(l2), .Q(r2), .clk(CLK), .clr(RST));
  Register #(.width(32)) register_9 (.D(DI), .en(l10), .Q(r10), .clk(CLK), .clr(RST));
  Register #(.width(32)) register_10 (.D(DI), .en(l18), .Q(r18), .clk(CLK), .clr(RST));
  Register #(.width(32)) register_11 (.D(DI), .en(l26), .Q(r26), .clk(CLK), .clr(RST));
  Register #(.width(32)) register_12 (.D(DI), .en(l3), .Q(r3), .clk(CLK), .clr(RST));
  Register #(.width(32)) register_13 (.D(DI), .en(l11), .Q(r11), .clk(CLK), .clr(RST));
  Register #(.width(32)) register_14 (.D(DI), .en(l19), .Q(r19), .clk(CLK), .clr(RST));
  Register #(.width(32)) register_15 (.D(DI), .en(l27), .Q(r27), .clk(CLK), .clr(RST));
  Multiplexer #(.select(5), .width(32), .enable("false")) multiplexer_1 (
    .in0({32{1'b0}}), .in1(r1), .in2(r2), .in3(r3), .in4(r4), .in5(r5), .in6(r6), .in7(r7), .in8(r8),
    .in9(r9), .in10(r10), .in11(r11), .in12(r12), .in13(r13), .in14(r14), .in15(r15), .in16(r16), .in17(r17),
    .in18(r18), .in19(r19), .in20(r20), .in21(r21), .in22(r22), .in23(r23), .in24(r24), .in25(r25),
    .in26(r26), .in27(r27), .in28(r28), .in29(r29), .in30(r30), .in31(r31), .out(A), .sel(SA));
  Register #(.width(32)) register_16 (.D(DI), .en(l4), .Q(r4), .clk(CLK), .clr(RST));
  Register #(.width(32)) register_17 (.D(DI), .en(l12), .Q(r12), .clk(CLK), .clr(RST));
  Register #(.width(32)) register_18 (.D(DI), .en(l20), .Q(r20), .clk(CLK), .clr(RST));
  Register #(.width(32)) register_19 (.D(DI), .en(l28), .Q(r28), .clk(CLK), .clr(RST));
  Register #(.width(32)) register_20 (.D(DI), .en(l5), .Q(r5), .clk(CLK), .clr(RST));
  Register #(.width(32)) register_21 (.D(DI), .en(l13), .Q(r13), .clk(CLK), .clr(RST));
  Register #(.width(32)) register_22 (.D(DI), .en(l21), .Q(r21), .clk(CLK), .clr(RST));
  Register #(.width(32)) register_23 (.D(DI), .en(l29), .Q(r29), .clk(CLK), .clr(RST));
  Register #(.width(32)) register_24 (.D(DI), .en(l6), .Q(r6), .clk(CLK), .clr(RST));
  Register #(.width(32)) register_25 (.D(DI), .en(l14), .Q(r14), .clk(CLK), .clr(RST));
  Register #(.width(32)) register_26 (.D(DI), .en(l22), .Q(r22), .clk(CLK), .clr(RST));
  Register #(.width(32)) register_27 (.D(DI), .en(l30), .Q(r30), .clk(CLK), .clr(RST));
  Multiplexer #(.select(5), .width(32), .enable("false")) multiplexer_2 (
    .in0({32{1'b0}}), .in1(r1), .in2(r2), .in3(r3), .in4(r4), .in5(r5), .in6(r6), .in7(r7), .in8(r8),
    .in9(r9), .in10(r10), .in11(r11), .in12(r12), .in13(r13), .in14(r14), .in15(r15), .in16(r16), .in17(r17),
    .in18(r18), .in19(r19), .in20(r20), .in21(r21), .in22(r22), .in23(r23), .in24(r24), .in25(r25),
    .in26(r26), .in27(r27), .in28(r28), .in29(r29), .in30(r30), .in31(r31), .out(B), .sel(SB));
  Register #(.width(32)) register_28 (.D(DI), .en(l7), .Q(r7), .clk(CLK), .clr(RST));
  Register #(.width(32)) register_29 (.D(DI), .en(l15), .Q(r15), .clk(CLK), .clr(RST));
  Register #(.width(32)) register_30 (.D(DI), .en(l23), .Q(r23), .clk(CLK), .clr(RST));
  SP sp_1 (.di(DI), .l(l31), .r31(r31), .c(CLK), .r(RST), .push(push), .pop(pop));

  // Other names for the same wires on the sheet: c = CLK; r = RST
endmodule

module SP (
  input  push,
  input  pop,
  input  [31:0] di,
  input  l,
  input  c,
  input  r,
  output [31:0] r31
);

  wire reg0op1, sum1sub0;
  wire [31:0] adder_1_out, multiplexer_1_out, opp, subtractor_1_out;

  sumrestsp sumrestsp_1 (.push(push), .pop(pop), .sumrest(sum1sub0), .sumrestreg(reg0op1));
  Multiplexer #(.width(32), .disabled(0), .enable("false")) multiplexer_1 (
    .in0(di), .in1(opp), .out(multiplexer_1_out), .sel(reg0op1));
  Register #(.width(32)) register_1 (.D(multiplexer_1_out), .en(l), .Q(r31), .clk(c), .clr(r));
  Adder #(.width(32)) adder_1 (.a(r31), .b(32'h4), .out(adder_1_out));  // open: cin, cout
  Subtractor #(.width(32)) subtractor_1 (.a(r31), .b(32'h4), .out(subtractor_1_out));  // open: bin, bout
  Multiplexer #(.width(32), .disabled(0), .enable("false")) multiplexer_2 (
    .in0(subtractor_1_out), .in1(adder_1_out), .out(opp), .sel(sum1sub0));
endmodule

module ALU (
  input  [31:0] A,
  input  [31:0] B,
  input  clk,
  input  [3:0] SEL,
  output [31:0] out_5
);

  wire comparator_1_lt, comparator_2_lt, hilo;
  wire [1:0] hisel;
  wire [31:0] \and , divuhi, divulo, hi, low, multiplexer_2_out, multiplexer_3_out, muluhi, mululo, \nor ,
       \or , slt, sltu, tunnel, tunnel_t, \xor ;

  Adder #(.width(32)) adder_1 (.a(A), .b(B), .out(tunnel));  // open: cin, cout
  Subtractor #(.width(32)) subtractor_1 (.a(A), .b(B), .out(tunnel_t));  // open: bin, bout
  Multiplier #(.width(32)) multiplier_1 (.a(A), .b(B), .out(mululo), .cout(muluhi));  // open: cin
  Divider #(.width(32)) divider_1 (.a(A), .b(B), .out(divulo), .rem(divuhi));  // open: upper
  Comparator #(.width(32)) comparator_1 (.a(A), .b(B), .lt(comparator_1_lt));  // open: gt, eq
  Comparator #(.width(32), .mode("unsigned")) comparator_2 (.a(A), .b(B), .lt(comparator_2_lt));  // open: gt, eq
  concat concat_1 (.in_1(comparator_1_lt), .Output(slt));
  concat concat_2 (.in_1(comparator_2_lt), .Output(sltu));
  assign \and  = A & B;  // AND_Gate and_1, 32 bits wide
  assign \or  = A | B;  // OR_Gate or_1, 32 bits wide
  assign \nor  = ~(A | B);  // NOR_Gate nor_1, 32 bits wide
  assign \xor  = A ^ B;  // XOR_Gate xor_1, 32 bits wide
  Multiplexer #(.select(4), .width(32), .enable("false")) multiplexer_1 (
    .in1(tunnel), .in2(tunnel_t), .in7(slt), .in8(sltu), .in9(\and ), .in10(\or ), .in11(\nor ),
    .in12(\xor ), .in13(A), .in14(hi), .in15(low), .out(out_5), .sel(SEL));  // open: in0, in3, in4, in5, in6
  Multiplexer #(.select(2), .width(32), .enable("false")) multiplexer_2 (
    .in1(muluhi), .in3(divuhi), .out(multiplexer_2_out), .sel(hisel));  // open: in0, in2
  Multiplexer #(.select(2), .width(32), .enable("false")) multiplexer_3 (
    .in1(mululo), .in3(divulo), .out(multiplexer_3_out), .sel(hisel));  // open: in0, in2
  mulu_divu mulu_divu_1 (.in_1(SEL), .Output(hisel));
  hilo hilo_1 (.in_1(SEL), .divmul(hilo));
  Register #(.width(32)) register_1 (.D(multiplexer_2_out), .en(hilo), .Q(hi), .clk(clk));  // open: clr
  Register #(.width(32)) register_2 (.D(multiplexer_3_out), .en(hilo), .Q(low), .clk(clk));  // open: clr

  // Other names for the same wires on the sheet: c = clk
endmodule

module InstSeparator (
  input  [31:0] in_1,
  output [5:0] OPcode,
  output [4:0] Rs,
  output [4:0] Rt,
  output [4:0] Rd,
  output [4:0] x,
  output [5:0] FUNCode
);


  assign FUNCode = in_1[5:0];
  assign OPcode = in_1[31:26];
  assign Rd = in_1[15:11];
  assign Rs = in_1[25:21];
  assign Rt = in_1[20:16];
  assign x = in_1[10:6];
endmodule

module OPDECODE (
  input  [5:0] in_1,
  output [1:0] Output
);

  wire and_1_out, and_2_out, and_3_out, and_4_out, and_5_out, not_1_out, not_2_out, not_3_out, not_4_out,
       not_5_out, not_6_out;

  not not_1 (not_1_out, in_1[2]);
  not not_2 (not_2_out, in_1[1]);
  not not_3 (not_3_out, in_1[0]);
  not not_4 (not_4_out, in_1[5]);
  not not_5 (not_5_out, in_1[3]);
  not not_6 (not_6_out, in_1[4]);
  and and_1 (and_1_out, in_1[5], in_1[4], in_1[3], not_1_out, not_2_out, not_3_out);
  and and_2 (and_2_out, in_1[5], in_1[4], in_1[3], in_1[2], in_1[1], in_1[0]);
  and and_3 (and_3_out, not_4_out, in_1[3]);
  and and_4 (and_4_out, in_1[4], not_5_out);
  and and_5 (and_5_out, in_1[5], not_6_out);
  or or_1 (Output[1], and_1_out, and_2_out);
  or or_2 (Output[0], in_1[0], in_1[1], in_1[2], and_3_out, and_4_out, and_5_out);
endmodule

module FUNC000000DECODE (
  input  [5:0] in_1,
  output [3:0] Output
);

  wire and_1_out, and_2_out, and_3_out, and_4_out, and_5_out, and_6_out, and_7_out, and_8_out, and_9_out,
       and_10_out, and_11_out, and_12_out, and_13_out, and_14_out, and_15_out, and_16_out, and_17_out,
       and_18_out, and_19_out, and_20_out, not_1_out, not_2_out, not_3_out, not_4_out, not_5_out, not_6_out,
       not_7_out, not_8_out, not_9_out, not_10_out, not_11_out, not_12_out, not_13_out, not_14_out,
       not_15_out, not_16_out, not_17_out, not_18_out, not_19_out, not_20_out, not_21_out, not_22_out,
       not_23_out, not_24_out, not_25_out, not_26_out, not_27_out, not_28_out, not_29_out, not_30_out,
       not_31_out, not_32_out, not_33_out, not_34_out, not_35_out, not_36_out, not_37_out, not_38_out,
       not_39_out, not_40_out, not_41_out, not_42_out, not_43_out, not_44_out, not_45_out, not_46_out,
       not_47_out, not_48_out, not_49_out, not_50_out, not_51_out, not_52_out, not_53_out, not_54_out,
       not_55_out, not_56_out, not_57_out, not_58_out, not_59_out, not_60_out, not_61_out, not_62_out;

  not not_1 (not_1_out, in_1[4]);
  not not_2 (not_2_out, in_1[2]);
  not not_3 (not_3_out, in_1[1]);
  not not_4 (not_4_out, in_1[0]);
  not not_5 (not_5_out, in_1[5]);
  not not_6 (not_6_out, in_1[3]);
  not not_7 (not_7_out, in_1[2]);
  not not_8 (not_8_out, in_1[0]);
  not not_9 (not_9_out, in_1[4]);
  not not_10 (not_10_out, in_1[3]);
  not not_11 (not_11_out, in_1[1]);
  not not_12 (not_12_out, in_1[4]);
  not not_13 (not_13_out, in_1[3]);
  not not_14 (not_14_out, in_1[4]);
  not not_15 (not_15_out, in_1[2]);
  not not_16 (not_16_out, in_1[4]);
  not not_17 (not_17_out, in_1[2]);
  not not_18 (not_18_out, in_1[1]);
  not not_19 (not_19_out, in_1[0]);
  not not_20 (not_20_out, in_1[5]);
  not not_21 (not_21_out, in_1[3]);
  not not_22 (not_22_out, in_1[2]);
  not not_23 (not_23_out, in_1[0]);
  not not_24 (not_24_out, in_1[5]);
  not not_25 (not_25_out, in_1[2]);
  not not_26 (not_26_out, in_1[0]);
  not not_27 (not_27_out, in_1[5]);
  not not_28 (not_28_out, in_1[2]);
  not not_29 (not_29_out, in_1[4]);
  not not_30 (not_30_out, in_1[2]);
  not not_31 (not_31_out, in_1[0]);
  not not_32 (not_32_out, in_1[5]);
  not not_33 (not_33_out, in_1[3]);
  not not_34 (not_34_out, in_1[2]);
  not not_35 (not_35_out, in_1[0]);
  not not_36 (not_36_out, in_1[5]);
  not not_37 (not_37_out, in_1[2]);
  not not_38 (not_38_out, in_1[1]);
  not not_39 (not_39_out, in_1[0]);
  not not_40 (not_40_out, in_1[5]);
  not not_41 (not_41_out, in_1[2]);
  not not_42 (not_42_out, in_1[4]);
  not not_43 (not_43_out, in_1[2]);
  not not_44 (not_44_out, in_1[0]);
  not not_45 (not_45_out, in_1[4]);
  not not_46 (not_46_out, in_1[3]);
  not not_47 (not_47_out, in_1[5]);
  not not_48 (not_48_out, in_1[2]);
  not not_49 (not_49_out, in_1[1]);
  not not_50 (not_50_out, in_1[0]);
  not not_51 (not_51_out, in_1[5]);
  not not_52 (not_52_out, in_1[2]);
  not not_53 (not_53_out, in_1[0]);
  not not_54 (not_54_out, in_1[4]);
  not not_55 (not_55_out, in_1[3]);
  not not_56 (not_56_out, in_1[1]);
  not not_57 (not_57_out, in_1[0]);
  not not_58 (not_58_out, in_1[4]);
  not not_59 (not_59_out, in_1[3]);
  not not_60 (not_60_out, in_1[4]);
  not not_61 (not_61_out, in_1[2]);
  not not_62 (not_62_out, in_1[0]);
  and and_1 (and_1_out, not_1_out, in_1[3], not_2_out, not_3_out, not_4_out);
  and and_2 (and_2_out, not_5_out, in_1[4], not_6_out, not_7_out, not_8_out);
  and and_3 (and_3_out, in_1[5], not_9_out, not_10_out, in_1[2], not_11_out);
  and and_4 (and_4_out, in_1[5], not_12_out, not_13_out, in_1[2], in_1[0]);
  and and_5 (and_5_out, in_1[5], not_14_out, in_1[3], not_15_out, in_1[1], in_1[0]);
  and and_6 (and_6_out, not_16_out, in_1[3], not_17_out, not_18_out, not_19_out);
  and and_7 (and_7_out, not_20_out, in_1[4], not_21_out, not_22_out, not_23_out);
  and and_8 (and_8_out, not_24_out, in_1[4], not_25_out, in_1[1], not_26_out);
  and and_9 (and_9_out, not_27_out, in_1[4], in_1[3], not_28_out, in_1[0]);
  and and_10 (and_10_out, in_1[5], not_29_out, in_1[3], not_30_out, not_31_out);
  and and_11 (and_11_out, not_32_out, in_1[4], not_33_out, not_34_out, not_35_out);
  and and_12 (and_12_out, not_36_out, in_1[4], not_37_out, not_38_out, not_39_out);
  and and_13 (and_13_out, not_40_out, in_1[4], in_1[3], not_41_out, in_1[1], in_1[0]);
  and and_14 (and_14_out, in_1[5], not_42_out, not_43_out, in_1[1], not_44_out);
  and and_15 (and_15_out, in_1[5], not_45_out, not_46_out, in_1[2], in_1[0]);
  and and_16 (and_16_out, not_47_out, in_1[3], not_48_out, not_49_out, not_50_out);
  and and_17 (and_17_out, not_51_out, in_1[4], not_52_out, in_1[1], not_53_out);
  and and_18 (and_18_out, in_1[5], not_54_out, not_55_out, not_56_out, not_57_out);
  and and_19 (and_19_out, in_1[5], not_58_out, not_59_out, in_1[2], in_1[1], in_1[0]);
  and and_20 (and_20_out, in_1[5], not_60_out, in_1[3], not_61_out, in_1[1], not_62_out);
  or or_1 (Output[3], and_1_out, and_2_out, and_3_out, and_4_out, and_5_out);
  or or_2 (Output[2], and_6_out, and_7_out, and_8_out, and_9_out, and_10_out);
  or or_3 (Output[1], and_11_out, and_12_out, and_13_out, and_14_out, and_15_out);
  or or_4 (Output[0], and_16_out, and_17_out, and_18_out, and_19_out, and_20_out);
endmodule

module OPDisctinctDECODE (
  input  [5:0] in_1,
  output [3:0] Output
);

  wire and_1_out, and_2_out, and_3_out, and_5_out, and_6_out, and_7_out, and_8_out, not_1_out, not_2_out,
       not_3_out, not_4_out, not_5_out, not_6_out, not_7_out, not_8_out, not_9_out, not_10_out, not_11_out,
       not_12_out, not_13_out, not_14_out, not_15_out, not_16_out, not_17_out, not_18_out, not_19_out,
       not_20_out, not_21_out, not_22_out, not_23_out, not_24_out, not_25_out, not_26_out, not_27_out;

  not not_1 (not_1_out, in_1[5]);
  not not_2 (not_2_out, in_1[4]);
  not not_3 (not_3_out, in_1[2]);
  not not_4 (not_4_out, in_1[5]);
  not not_5 (not_5_out, in_1[4]);
  not not_6 (not_6_out, in_1[1]);
  not not_7 (not_7_out, in_1[5]);
  not not_8 (not_8_out, in_1[4]);
  not not_9 (not_9_out, in_1[0]);
  not not_10 (not_10_out, in_1[5]);
  not not_11 (not_11_out, in_1[4]);
  not not_12 (not_12_out, in_1[0]);
  not not_13 (not_13_out, in_1[5]);
  not not_14 (not_14_out, in_1[4]);
  not not_15 (not_15_out, in_1[2]);
  not not_16 (not_16_out, in_1[0]);
  not not_17 (not_17_out, in_1[5]);
  not not_18 (not_18_out, in_1[4]);
  not not_19 (not_19_out, in_1[1]);
  not not_20 (not_20_out, in_1[5]);
  not not_21 (not_21_out, in_1[4]);
  not not_22 (not_22_out, in_1[2]);
  not not_23 (not_23_out, in_1[0]);
  not not_24 (not_24_out, in_1[5]);
  not not_25 (not_25_out, in_1[4]);
  not not_26 (not_26_out, in_1[1]);
  not not_27 (not_27_out, in_1[0]);
  and and_1 (and_1_out, not_1_out, not_2_out, in_1[3], not_3_out, in_1[1], in_1[0]);
  and and_2 (and_2_out, not_4_out, not_5_out, in_1[3], in_1[2], not_6_out);
  and and_3 (and_3_out, not_7_out, not_8_out, in_1[3], in_1[2], not_9_out);
  and and_4 (Output[2], not_10_out, not_11_out, in_1[3], in_1[1], not_12_out);
  and and_5 (and_5_out, not_13_out, not_14_out, in_1[3], not_15_out, in_1[1], not_16_out);
  and and_6 (and_6_out, not_17_out, not_18_out, in_1[3], in_1[2], not_19_out, in_1[0]);
  and and_7 (and_7_out, not_20_out, not_21_out, in_1[3], not_22_out, not_23_out);
  or or_1 (Output[0], and_7_out, and_8_out);
  and and_8 (and_8_out, not_24_out, not_25_out, in_1[3], not_26_out, not_27_out);
  or or_2 (Output[3], and_1_out, and_2_out, and_3_out);
  or or_3 (Output[1], and_5_out, and_6_out);
endmodule

module Const (
  input  \logic ,
  input  [4:0] in_2,
  input  [4:0] in_3,
  input  [5:0] in_4,
  output [31:0] Output
);

  Multiplexer #(.enable("false")) multiplexer_1 (.in0(in_2[4]), .in1(1'b0), .out(Output[31]), .sel(\logic ));

  assign Output[30:0] = {{15{Output[31]}}, in_2, in_3, in_4};
endmodule

module concat (
  input  in_1,
  output [31:0] Output
);


  assign Output = {{31{1'b0}}, in_1};
endmodule

module hilo (
  input  [3:0] in_1,
  output divmul
);

  wire and_1_out, and_2_out, and_3_out, not_1_out, not_2_out, not_3_out, not_4_out, not_5_out, not_6_out;

  not not_1 (not_1_out, in_1[3]);
  not not_2 (not_2_out, in_1[2]);
  not not_3 (not_3_out, in_1[3]);
  not not_4 (not_4_out, in_1[1]);
  not not_5 (not_5_out, in_1[3]);
  not not_6 (not_6_out, in_1[0]);
  and and_1 (and_1_out, not_1_out, not_2_out, in_1[1], in_1[0]);
  and and_2 (and_2_out, not_3_out, in_1[2], not_4_out);
  and and_3 (and_3_out, not_5_out, in_1[2], not_6_out);
  or or_1 (divmul, and_1_out, and_2_out, and_3_out);
endmodule

module mulu_divu (
  input  [3:0] in_1,
  output [1:0] Output
);

  wire and_1_out, and_2_out, not_1_out, not_2_out;

  not not_1 (not_1_out, in_1[1]);
  and and_1 (and_1_out, not_1_out, in_1[0]);
  and and_2 (and_2_out, in_1[1], not_2_out);
  not not_2 (not_2_out, in_1[0]);
  not not_3 (Output[0], in_1[0]);
  or or_1 (Output[1], and_1_out, and_2_out);
endmodule

module Writefromalu (
  input  [3:0] in_1,
  output write
);

  wire and_1_out, and_2_out, and_3_out, and_4_out, and_5_out, not_1_out, not_2_out, not_3_out, not_4_out,
       not_5_out, not_6_out;

  not not_1 (not_1_out, in_1[2]);
  not not_2 (not_2_out, in_1[1]);
  not not_3 (not_3_out, in_1[2]);
  not not_4 (not_4_out, in_1[0]);
  not not_5 (not_5_out, in_1[2]);
  not not_6 (not_6_out, in_1[0]);
  and and_1 (and_1_out, not_1_out, not_2_out, in_1[0]);
  and and_2 (and_2_out, not_3_out, in_1[1], not_4_out);
  and and_3 (and_3_out, in_1[2], in_1[1], in_1[0]);
  and and_4 (and_4_out, in_1[3], not_5_out);
  and and_5 (and_5_out, in_1[3], not_6_out);
  or or_1 (write, and_1_out, and_2_out, and_3_out, and_4_out, and_5_out);
endmodule

module awaiter (
  input  start,
  input  [3:0] in_2,
  input  clk,
  output \end 
);

  wire comparator_1_gt, or_1_out;
  wire [3:0] counter_1_q;

  or or_1 (or_1_out, start, comparator_1_gt);
  Counter #(.width(4), .max('hf), .ongoal("stay")) counter_1 (
    .load(or_1_out), .D(in_2), .count(comparator_1_gt), .Q(counter_1_q), .clk(clk));  // open: carry, clr
  Comparator #(.width(4), .mode("unsigned")) comparator_1 (
    .a(counter_1_q), .b(4'b0000), .gt(comparator_1_gt), .eq(\end ));  // open: lt
endmodule

module tests (
  input  [31:0] in_1,
  output [31:0] Output,
  output [4:0] Output_2
);

  Subtractor #(.width(32)) subtractor_1 (.a(in_1), .b(32'h4), .out(Output));  // open: bin, bout

  assign Output_2 = {5{1'b1}};
endmodule

module push_pop (
  input  [1:0] OP,
  input  [5:0] FUNC,
  output push,
  output pop
);

  wire and_1_out;

  and and_1 (and_1_out, OP[1], ~OP[0]);  // AND_Gate
  and and_2 (push, and_1_out, FUNC[0]);
  and and_3 (pop, and_1_out, ~FUNC[0]);  // AND_Gate
endmodule

module SMIPSTEST (
  input  Kbd_Available,
  input  [6:0] Kbd_ASCII_Data,
  input  [31:0] RAM_Out_0,
  input  [15:0] in_4,
  input  [31:0] RAM_Out_1,
  input  Reset,
  input  [31:0] RAM_Out_2,
  input  Clock,
  input  [31:0] RAM_Out_3,
  input  [3:0] Read_Time,
  input  [3:0] Write_Time,
  output Kbd_Enable,
  output [15:0] Address,
  output Kbd_Clear,
  output TTY_Enable,
  output [6:0] TTY_ASCII_Data,
  output Stop,
  output [31:0] RAM_In_0,
  output [31:0] RAM_In_1,
  output [31:0] RAM_In_2,
  output [31:0] RAM_In_3,
  output [3:0] Mask,
  output nRead_Write,
  output Chip_Select
);


  assign Address = in_4;

  // Other names for the same wires on the sheet: CLK = Clock; CLR = Reset; CS = Chip_Select;
  //   KBD_AVAIL = Kbd_Available; KBD_CLR = Kbd_Clear; KBD_DATA[6:0] = Kbd_ASCII_Data; RAM_A[15:0] = in_4;
  //   RAM_INPUT_0[31:0] = RAM_In_0; RAM_INPUT_1[31:0] = RAM_In_1; RAM_INPUT_2[31:0] = RAM_In_2;
  //   RAM_INPUT_3[31:0] = RAM_In_3; RAM_MASK[3:0] = Mask; RAM_OUTPUT_0[31:0] = RAM_Out_0;
  //   RAM_OUTPUT_1[31:0] = RAM_Out_1; RAM_OUTPUT_2[31:0] = RAM_Out_2; RAM_OUTPUT_3[31:0] = RAM_Out_3;
  //   RW = nRead_Write; TTY_DATA[6:0] = TTY_ASCII_Data

  // Notes on the sheet:
  //   RAM ADDRESS
  //   DATA FROM RAM
  //   DATA TO RAM
  //   DATA WRITE MASK
  //   RAM TIMING
  //   RAM CONTROL
  //   KEYBOARD
  //   TTY
  //   SEQUENCING
endmodule

module jr (
  input  [3:0] in_1,
  output jr
);

  wire not_1_out;

  not not_1 (not_1_out, in_1[1]);
  and and_1 (jr, in_1[3], in_1[2], not_1_out, in_1[0]);
endmodule

module sumrestsp (
  input  push,
  input  pop,
  output sumrest,
  output sumrestreg
);

  wire and_2_out, and_3_out, not_1_out, not_2_out, not_3_out;

  not not_1 (not_1_out, push);
  not not_2 (not_2_out, push);
  not not_3 (not_3_out, pop);
  and and_1 (sumrest, not_1_out, pop);
  and and_2 (and_2_out, not_2_out, pop);
  and and_3 (and_3_out, push, not_3_out);
  or or_1 (sumrestreg, and_2_out, and_3_out);
endmodule

module Offst (
  input  [4:0] in_1,
  input  [4:0] in_2,
  input  [5:0] in_3,
  output [31:0] Output
);


  assign Output = {{15{in_1[4]}}, in_1[3:0], in_2, in_3, 2'b00};
endmodule

module islogic (
  input  [3:0] in_1,
  output islogic
);

  wire and_1_out, and_2_out, and_3_out, not_1_out, not_2_out, not_3_out, not_4_out;

  not not_1 (not_1_out, in_1[1]);
  not not_2 (not_2_out, in_1[0]);
  not not_3 (not_3_out, in_1[2]);
  and and_1 (and_1_out, in_1[3], not_3_out, in_1[0]);
  not not_4 (not_4_out, in_1[2]);
  and and_2 (and_2_out, in_1[3], not_4_out, in_1[1]);
  and and_3 (and_3_out, in_1[3], in_1[2], not_1_out, not_2_out);
  or or_1 (islogic, and_1_out, and_2_out, and_3_out);
endmodule

module branch (
  input  [5:0] in_1,
  output beq,
  output bne,
  output blez,
  output bgtz,
  output bltz,
  output j
);

  wire not_1_out, not_2_out, not_3_out, not_4_out, not_5_out, not_6_out, not_7_out, not_8_out, not_9_out,
       not_10_out, not_11_out, not_12_out, not_13_out, not_14_out, not_15_out, not_16_out, not_17_out,
       not_18_out, not_19_out, not_20_out, not_21_out, not_22_out, not_23_out, not_24_out, not_25_out,
       not_26_out;

  not not_1 (not_1_out, in_1[5]);
  not not_2 (not_2_out, in_1[4]);
  not not_3 (not_3_out, in_1[3]);
  not not_4 (not_4_out, in_1[1]);
  not not_5 (not_5_out, in_1[0]);
  not not_6 (not_6_out, in_1[5]);
  not not_7 (not_7_out, in_1[4]);
  not not_8 (not_8_out, in_1[3]);
  not not_9 (not_9_out, in_1[1]);
  not not_10 (not_10_out, in_1[5]);
  not not_11 (not_11_out, in_1[4]);
  not not_12 (not_12_out, in_1[3]);
  not not_13 (not_13_out, in_1[0]);
  not not_14 (not_14_out, in_1[5]);
  not not_15 (not_15_out, in_1[4]);
  not not_16 (not_16_out, in_1[3]);
  not not_17 (not_17_out, in_1[5]);
  not not_18 (not_18_out, in_1[4]);
  not not_19 (not_19_out, in_1[3]);
  not not_20 (not_20_out, in_1[2]);
  not not_21 (not_21_out, in_1[1]);
  not not_22 (not_22_out, in_1[5]);
  not not_23 (not_23_out, in_1[4]);
  not not_24 (not_24_out, in_1[3]);
  not not_25 (not_25_out, in_1[2]);
  not not_26 (not_26_out, in_1[0]);
  and and_1 (beq, not_1_out, not_2_out, not_3_out, in_1[2], not_4_out, not_5_out);
  and and_2 (bne, not_6_out, not_7_out, not_8_out, in_1[2], not_9_out, in_1[0]);
  and and_3 (blez, not_10_out, not_11_out, not_12_out, in_1[2], in_1[1], not_13_out);
  and and_4 (bgtz, not_14_out, not_15_out, not_16_out, in_1[2], in_1[1], in_1[0]);
  and and_5 (bltz, not_17_out, not_18_out, not_19_out, not_20_out, not_21_out, in_1[0]);
  and and_6 (j, not_22_out, not_23_out, not_24_out, not_25_out, in_1[1], not_26_out);
endmodule

module destinosalto (
  input  [5:0] fx,
  input  [4:0] x,
  input  [4:0] Rd,
  input  [4:0] Rt,
  input  [4:0] Rs,
  output [25:0] Output
);


  assign Output = {Rs, Rt, Rd, x, fx};
endmodule

module destinobuilder (
  input  [25:0] des,
  input  [31:0] PC,
  output [31:0] Output
);


  assign Output = {PC[31:28], des, 2'b00};
endmodule
